// Logisim project SystemSide_Draft.circ as structural Verilog: 1 circuit, main circuit main
module main (
  input  ON,
  output [7:0] out_2
);

  wire _0_out, _1_out, _2_out, _3_out, _4_out, _5_out, _6_out, _7_out, _8_out, _9_out, ALU_are_equal,
       and_1_out, and_2_out, and_3_out, and_4_out, and_5_out, and_6_out, and_7_out, and_8_out, clock_1_out,
       CU_p3, CU_p5, CU_p6, CU_p7, CU_p8, CU_p11, CU_p12, CU_p13, CU_p14, CU_p15, CU_p16, CU_p18, CU_p19,
       CU_p20, CU_p21, CU_p23, CU_p24, CU_p26, CU_p27, main_2_out_2, main_2_out_3, main_2_out_4,
       main_2_out_5, main_2_out_6, main_2_out_7, main_2_out_8, main_2_out_9, main_2_out_10, main_2_out_11,
       main_2_out_12, main_2_out_13, main_2_out_14, main_2_out_15, main_2_out_16, main_2_out_17,
       main_2_out_18, main_2_out_19, main_2_out_20, main_2_out_21, main_2_out_22, not_1_out, not_2_out,
       not_3_out, not_4_out, not_5_out, not_6_out, or_2_out, or_3_out, or_4_out, or_5_out, or_6_out,
       or_7_out, or_8_out, or_9_out, or_10_out, or_11_out, or_12_out, or_13_out;
  wire [1:0] CU_p9, CU_p17, or_1_out;
  wire [3:0] IR_output, main_4_output, MAR_output, multiplexer_3_out, multiplexer_5_out, multiplexer_8_out;
  wire [7:0] ALU_result, keypadblackbox_1_p11, L_output, main_1_out, main_3_p3, MBR_output,
       multiplexer_1_out, multiplexer_4_out, multiplexer_6_out, multiplexer_7_out, multiplexer_9_out,
       multiplexer_10_out, R0_output, R1_output, R_output, register_1_output;
  wire [7:4] IR_output_2;

  Clock clock_1 (.out(clock_1_out));
  _7_Segment_Display u_7_segment_display_1 (
    .g(main_2_out_17), .f(main_2_out_18), .a(main_2_out_2), .b(main_2_out_5), .e(main_2_out_14),
    .d(main_2_out_11), .c(main_2_out_8));  // open: dp
  Button _1 (.out(_1_out));
  Button _4 (.out(_4_out));
  Button _7 (.out(_7_out));
  _7_Segment_Display u_7_segment_display_2 (
    .g(main_2_out_19), .f(main_2_out_20), .a(main_2_out_3), .b(main_2_out_6), .e(main_2_out_15),
    .d(main_2_out_12), .c(main_2_out_9));  // open: dp
  not not_1 (not_1_out, ON);
  Multiplexer #(.width(8), .enable("false")) multiplexer_1 (
    .in0(out_2), .in1(keypadblackbox_1_p11), .out(multiplexer_1_out), .sel(or_1_out[1]));
  Button _2 (.out(_2_out));
  Button _5 (.out(_5_out));
  Button _8 (.out(_8_out));
  Button _0 (.out(_0_out));
  Button _3 (.out(_3_out));
  Button _6 (.out(_6_out));
  Button _9 (.out(_9_out));
  // keypadblackbox keypadblackbox_1: pin names not known; wires that end beside it: _0_out, _1_out, _2_out, _3_out, _4_out, _5_out, _6_out, _7_out, _8_out, _9_out, keypadblackbox_1_p11
  _7_Segment_Display u_7_segment_display_3 (
    .g(main_2_out_21), .f(main_2_out_22), .a(main_2_out_4), .b(main_2_out_7), .e(main_2_out_16),
    .d(main_2_out_13), .c(main_2_out_10));  // open: dp
  Pete_RAM_main main_1 (
    .Clock(clock_1_out), .R_W(or_2_out), .Address(multiplexer_3_out), .Data(multiplexer_1_out),
    .Clear(not_1_out), .Out(main_1_out));
  // Probe on keypadblackbox_1_p11
  // Probe on main_1_out
  // Probe on multiplexer_3_out
  _8bitTo3dec_main main_2 (
    .out_19(main_2_out_19), .out_20(main_2_out_20), .out_15(main_2_out_15), .out_9(main_2_out_9),
    .out_12(main_2_out_12), .out_6(main_2_out_6), .out_3(main_2_out_3), .out_4(main_2_out_4),
    .out_7(main_2_out_7), .out_10(main_2_out_10), .out_13(main_2_out_13), .out_16(main_2_out_16),
    .out_21(main_2_out_21), .out_22(main_2_out_22), .out_2(main_2_out_2), .out_5(main_2_out_5),
    .out_8(main_2_out_8), .out_11(main_2_out_11), .out_14(main_2_out_14), .out_17(main_2_out_17),
    .out_18(main_2_out_18), .in_1(out_2));
  Multiplexer #(.select(2), .width(8), .enable("false")) multiplexer_2 (
    .in0(main_1_out), .in1(MBR_output), .in2(keypadblackbox_1_p11), .out(out_2), .sel(or_1_out));  // open: in3
  or or_1 (or_1_out[0], CU_p20, CU_p11);
  // Probe on MBR_output
  Multiplexer #(.width(4), .enable("false")) multiplexer_3 (
    .in0(MAR_output), .in1(4'b1111), .out(multiplexer_3_out), .sel(or_11_out));
  or or_2 (or_2_out, or_1_out[1], CU_p20, CU_p11, CU_p21);
  Multiplexer #(.select(2), .width(8), .enable("false")) multiplexer_4 (
    .in0(out_2), .in1(R0_output), .in2(R1_output), .out(multiplexer_4_out), .sel(CU_p9));  // open: in3
  Multiplexer #(.width(4), .enable("false")) multiplexer_5 (
    .in0(main_4_output), .in1(IR_output), .out(multiplexer_5_out), .sel(CU_p8));
  not not_2 (not_2_out, IR_output[1]);
  Multiplexer #(.select(2), .width(8), .enable("false")) multiplexer_6 (
    .in0(MBR_output), .in1(ALU_result), .in3(register_1_output), .out(multiplexer_6_out), .sel(CU_p17));  // open: in2
  Multiplexer #(.select(2), .width(8), .enable("false")) multiplexer_7 (
    .in0(MBR_output), .in1(ALU_result), .in2(register_1_output), .out(multiplexer_7_out), .sel(CU_p17));  // open: in3
  or or_3 (or_3_out, CU_p23, CU_p9[1], CU_p9[0], CU_p7);
  // Probe on R0_output
  // Probe on R1_output
  and and_1 (and_1_out, not_2_out, CU_p17[0]);
  and and_2 (and_2_out, IR_output[1], CU_p17[0]);
  and and_3 (and_3_out, IR_output[1], CU_p17[1]);
  not not_3 (not_3_out, IR_output[1]);
  and and_4 (and_4_out, not_3_out, CU_p17[1]);
  _4_bit_register__MAR MAR (.Clock(clock_1_out), .R_0__W_1(or_4_out), .Input(multiplexer_5_out), .Output(MAR_output));
  or or_4 (or_4_out, CU_p5, CU_p8);
  Register MBR (.Clock(clock_1_out), .R_0__W_1(or_3_out), .Input(multiplexer_4_out), .Output(MBR_output));
  or or_5 (or_5_out, CU_p14, and_1_out, and_3_out);
  Register R0 (.Clock(clock_1_out), .R_0__W_1(or_5_out), .Input(multiplexer_6_out), .Output(R0_output));
  or or_6 (or_6_out, and_4_out, and_2_out, CU_p15);
  Register R1 (.Clock(clock_1_out), .R_0__W_1(or_6_out), .Input(multiplexer_7_out), .Output(R1_output));
  // Probe on MBR_output
  or or_7 (or_7_out, CU_p6, or_12_out);
  Multiplexer #(.width(4), .enable("false")) multiplexer_8 (
    .in0(main_4_output), .in1(IR_output), .out(multiplexer_8_out), .sel(or_10_out));
  or or_8 (or_8_out, CU_p3, IR_output[3]);
  // multiply_main main_3: pin names not known; wires that end beside it: R0_output, R1_output, main_3_p3
  // Probe on main_4_output
  programcounter__alec_main main_4 (
    .activate(or_7_out), .INC_0__SET_1(or_10_out), .in_3(multiplexer_8_out), .\output (main_4_output));
  // Probe on multiplexer_9_out
  Multiplexer #(.width(8), .enable("false")) multiplexer_9 (
    .in0(R0_output), .in1(R1_output), .out(multiplexer_9_out), .sel(IR_output[2]));
  Multiplexer #(.width(8), .enable("false")) multiplexer_10 (
    .in0(R0_output), .in1(R1_output), .out(multiplexer_10_out), .sel(or_8_out));
  // Probe on multiplexer_10_out
  Register register_1 (.Clock(clock_1_out), .R_0__W_1(CU_p24), .Input(main_3_p3), .Output(register_1_output));
  Register IR (.Clock(clock_1_out), .R_0__W_1(CU_p6), .Input(MBR_output), .Output({IR_output_2, IR_output}));
  or or_9 (or_9_out, not_4_out, CU_p13);
  Register L (.Clock(clock_1_out), .R_0__W_1(CU_p16), .Input(multiplexer_9_out), .Output(L_output));
  Register R (.Clock(clock_1_out), .R_0__W_1(CU_p16), .Input(multiplexer_10_out), .Output(R_output));
  // Probe on ALU_result
  alu_main ALU (
    .A(L_output), .B(R_output), .Add_0_Sub_1(or_9_out), .are_equal(ALU_are_equal), .Result(ALU_result),
    .in_2(clock_1_out), .R_W(or_13_out));  // open: Zero, Carry, Overflow, Negative
  and and_5 (and_5_out, CU_p19, not_5_out);
  or or_10 (or_10_out, and_5_out, and_6_out);
  not not_4 (not_4_out, CU_p12);
  not not_5 (not_5_out, ALU_are_equal);
  and and_6 (and_6_out, ALU_are_equal, CU_p18);
  // CU CU: pin names not known; wires that end beside it: clock_1_out, IR_output_2, CU_p3, ON, CU_p5, CU_p6, CU_p7, CU_p8, CU_p9[0], CU_p9[1], CU_p11, CU_p12, CU_p13, CU_p14, CU_p15, CU_p16, CU_p17[0], CU_p18, CU_p19, CU_p20, CU_p21, or_1_out[1], CU_p23, CU_p24, CU_p17[1], CU_p26, CU_p27
  or or_11 (or_11_out, CU_p23, or_1_out[1], CU_p21, CU_p20);
  and and_7 (and_7_out, CU_p27, not_6_out);
  or or_12 (or_12_out, and_7_out, and_8_out);
  not not_6 (not_6_out, ALU_are_equal);
  and and_8 (and_8_out, ALU_are_equal, CU_p26);
  or or_13 (or_13_out, CU_p12, CU_p13);

  // Notes on the sheet:
  //   RAM(0)/MBR(1)/Keypad(2) to bus
  //   data 8-bit
  //   Address
  //   r(0)/w(1)
  //   MBR(0)/Keypad(1) to RAM
endmodule
