// Logisim project programcounter__alec.circ as structural Verilog: 1 circuit, main circuit main
module main (
  input  activate,
  input  INC_0__SET_1,
  input  [3:0] in_3,
  output [3:0] \output 
);

  wire [3:0] adder_1_out, d_ff_1_q, multiplexer_1_out;

  // Probe on adder_1_out
  Adder #(.width(4)) adder_1 (.a(\output ), .b(4'b0001), .out(adder_1_out));  // open: cin, cout
  D_Flip_Flop d_ff_1 (.clk(activate), .D(in_3[0]), .Q(d_ff_1_q[0]));  // open: Qn, preset, en, reset
  D_Flip_Flop d_ff_2 (.clk(activate), .D(in_3[1]), .Q(d_ff_1_q[1]));  // open: Qn, preset, en, reset
  D_Flip_Flop d_ff_3 (.clk(activate), .D(in_3[2]), .Q(d_ff_1_q[2]));  // open: Qn, preset, en, reset
  D_Flip_Flop d_ff_4 (.clk(activate), .D(in_3[3]), .Q(d_ff_1_q[3]));  // open: Qn, preset, en, reset
  Multiplexer #(.width(4), .enable("false")) multiplexer_1 (
    .in0(adder_1_out), .in1(d_ff_1_q), .out(multiplexer_1_out), .sel(INC_0__SET_1));
  D_Flip_Flop d_ff_5 (.clk(activate), .D(multiplexer_1_out[3]), .Q(\output [0]));  // open: Qn, preset, en, reset
  D_Flip_Flop d_ff_6 (.clk(activate), .D(multiplexer_1_out[2]), .Q(\output [1]));  // open: Qn, preset, en, reset
  D_Flip_Flop d_ff_7 (.clk(activate), .D(multiplexer_1_out[1]), .Q(\output [2]));  // open: Qn, preset, en, reset
  D_Flip_Flop d_ff_8 (.clk(activate), .D(multiplexer_1_out[0]), .Q(\output [3]));  // open: Qn, preset, en, reset
endmodule
